# Fritzing sketch LoRaWANTTNNode (saved by Fritzing 0.9.3b)

parts:
  WeMos_D1_Mini1 = WeMos D1 Mini
  RFM1 = RFM69HCW ISM Transciever
  RHT1 = Humidity and Temperature Sensor RHT03
  R1 = Photocell (LDR) [package=THT]
  R2 = Resistor [tolerance=±5% resistance=220 package="2010 [SMD]"]
  R3 = Resistor [tolerance=±5% resistance=220 package="2010 [SMD]"]
  R4 = Resistor [tolerance=±5% resistance=220 package="1206 [SMD]"]
  R6 = Resistor [tolerance=±5% resistance=220 package="0402 [SMD]"]
  LED3 = LED - 3mm [color="Red (633nm)" package="3 mm [THT]"]
  ANT1 = Antenna
  R7 = Resistor [tolerance=±5% resistance=220 package="2010 [SMD]"]

nets:
  3V3: WeMos_D1_Mini1.3V3, RFM1.13_3.3V, RHT1.Vcc, R2.Pin_1, R4.Pin_1
  N1: WeMos_D1_Mini1.A0, R1.pin_1, R7.Pin_0
  N2: WeMos_D1_Mini1.D0, R6.Pin_1
  N3: WeMos_D1_Mini1.D1, RFM1.14_DIO0
  N4: WeMos_D1_Mini1.D2, RFM1.15_DIO1
  N5: WeMos_D1_Mini1.D4, RHT1.Data-signal, R4.Pin_0
  N6: WeMos_D1_Mini1.D5, RFM1.4_SCK
  N7: WeMos_D1_Mini1.D6, RFM1.2_MISO
  N8: WeMos_D1_Mini1.D7, RFM1.3_MOSI
  N9: WeMos_D1_Mini1.D8, RFM1.5_NSS_(CS)
  GND: WeMos_D1_Mini1.G, RFM1.8_GND, RHT1.GND_2, R3.Pin_0, LED3.cathode, R7.Pin_1
  N10: RFM1.9_ANT, ANT1.antenna_lead
  N11: R1.pin_0, R2.Pin_0, R3.Pin_1
  N12: R6.Pin_0, LED3.anode

notes:
  1v divider with 1K and 2K2 resistors
  4K7 resistor with LDR to measure light between 0-1v
  RFM96 used for 868Mhz

custom parts:
  WeMos D1 Mini: The D1 mini is a mini wifi board based on ESP-8266EX.
  RFM69HCW ISM Transciever: RF Transceiver by Hope RF. Well supported Arduino libraries are available. This ISM band transceiver is available in several frequencies e.g. 433MHz and 915MHz and it is also available in various feature versions.
